// Logisim project control.circ as structural Verilog: 1 circuit, main circuit main
// Control
module main (
  input  Write,
  input  Clock,
  input  Clear,
  input  Enable,
  output Shift_Right,
  output Cycle,
  output End,
  output [7:0] out_8
);

  wire and_1_out, not_1_out, or_1_out;
  wire [7:0] adder_1_out;

  and and_1 (and_1_out, Enable, not_1_out);
  not not_1 (not_1_out, End);
  and and_2 (Cycle, and_1_out, Clock);
  and and_3 (Shift_Right, Write, Clock);
  or or_1 (or_1_out, Clear, End);
  Register register_1 (.D(adder_1_out), .Q(out_8), .clk(Cycle), .clr(or_1_out));  // open: en
  Adder adder_1 (.a(out_8), .b(8'h1), .out(adder_1_out));  // open: cin, cout
  Comparator comparator_1 (.a(out_8), .b(8'h21), .eq(End));  // open: gt, lt
endmodule
