// Logisim project datapath.circ as structural Verilog: 5 circuits, main circuit main
// Multiplier
module main (
  input  Set,
  input  [31:0] Multiplicand,
  input  [31:0] Multiplier,
  input  Clock,
  input  Clear,
  input  Enable,
  output [7:0] Counter,
  output [31:0] LSB,
  output [31:0] MSB
);

  wire bitselector_1_out, bitselector_2_out, main_1_cycle, main_1_end, main_1_shift_right, or_1_out,
       or_2_out, or_3_out;
  wire [31:0] msbsetter_1_output, multiplexer_1_out, multiplexer_2_out, multiplexer_3_out, n32bitadder_1_res,
       n32bitshifter_1_output, n32bitshifter_2_output, n32bitshifter_3_output, register_1_q, register_2_q;

  msbsetter msbsetter_1 (.\input (n32bitshifter_1_output), .Flag(bitselector_2_out), .\output (msbsetter_1_output));
  or or_1 (or_1_out, Enable, Clock);
  _32bitshifter u_32bitshifter_1 (.flag(1'b0), .\input (register_1_q), .\output (n32bitshifter_1_output));
  Multiplexer #(.width(32), .enable("false")) multiplexer_1 (
    .in0(Multiplier), .in1(msbsetter_1_output), .out(multiplexer_1_out), .sel(or_1_out));
  Multiplexer #(.width(32), .enable("false")) multiplexer_2 (
    .in0(Multiplicand), .in1(n32bitshifter_2_output), .out(multiplexer_2_out), .sel(or_1_out));
  or or_2 (or_2_out, Set, main_1_cycle);
  Register #(.width(32)) register_1 (.D(multiplexer_1_out), .Q(register_1_q), .clk(or_2_out), .clr(Clear));  // open: en
  Register #(.width(32)) register_2 (.D(multiplexer_2_out), .Q(register_2_q), .clk(or_2_out), .clr(Clear));  // open: en
  BitSelector #(.width(32)) bitselector_1 (.in(register_1_q), .out(bitselector_1_out), .sel({5{1'b0}}));
  _32bitadder u_32bitadder_1 (.A(register_2_q), .B(register_1_q), .Res(n32bitadder_1_res), .Ci(1'b0));
  _32bitshifter u_32bitshifter_2 (.flag(1'b0), .\input (register_2_q), .\output (n32bitshifter_2_output));
  BitSelector #(.width(32)) bitselector_2 (.in(register_2_q), .out(bitselector_2_out), .sel({5{1'b0}}));
  _32bitshifter u_32bitshifter_3 (.flag(1'b0), .\input (n32bitadder_1_res), .\output (n32bitshifter_3_output));
  Multiplexer #(.width(32)) multiplexer_3 (
    .in0(n32bitshifter_2_output), .in1(n32bitshifter_3_output), .out(multiplexer_3_out),
    .sel(main_1_shift_right), .en(main_1_cycle));
  control_main main_1 (
    .Write(bitselector_1_out), .Clock(Clock), .Clear(Clear), .Enable(Enable),
    .Shift_Right(main_1_shift_right), .End(main_1_end), .out_8(Counter), .Cycle(main_1_cycle));
  Register #(.width(32), .trigger("high")) register_3 (
    .D(multiplexer_3_out), .Q(MSB), .clk(Enable), .clr(or_3_out));  // open: en
  or or_3 (or_3_out, Clear, main_1_end);
  Register #(.width(32), .trigger("high")) register_4 (
    .D(msbsetter_1_output), .Q(LSB), .clk(Enable), .clr(or_3_out));  // open: en
endmodule

module fulladder (
  input  Ci,
  input  A,
  input  B,
  output Sum,
  output Ci_1
);

  wire and_1_out, and_2_out, and_3_out, not_1_out, not_2_out, or_1_out, or_2_out;

  or or_1 (or_1_out, A, B);
  and and_1 (and_1_out, B, A);
  not not_1 (not_1_out, and_1_out);
  and and_2 (and_2_out, or_1_out, not_1_out);
  or or_2 (or_2_out, Ci, and_2_out);
  and and_3 (and_3_out, Ci, and_2_out);
  not not_2 (not_2_out, and_3_out);
  or or_3 (Ci_1, and_3_out, and_1_out);
  and and_4 (Sum, or_2_out, not_2_out);
endmodule

// Adder
module _32bitadder (
  input  [31:0] A,
  input  [31:0] B,
  input  Ci,
  output [31:0] Res
);

  wire fulladder_2_ci_1, fulladder_3_ci_1, fulladder_4_ci_1, fulladder_5_ci_1, fulladder_6_ci_1,
       fulladder_7_ci_1, fulladder_8_ci_1, fulladder_9_ci_1, fulladder_10_ci_1, fulladder_11_ci_1,
       fulladder_12_ci_1, fulladder_13_ci_1, fulladder_14_ci_1, fulladder_15_ci_1, fulladder_16_ci_1,
       fulladder_17_ci_1, fulladder_18_ci_1, fulladder_19_ci_1, fulladder_20_ci_1, fulladder_21_ci_1,
       fulladder_22_ci_1, fulladder_23_ci_1, fulladder_24_ci_1, fulladder_25_ci_1, fulladder_26_ci_1,
       fulladder_27_ci_1, fulladder_28_ci_1, fulladder_29_ci_1, fulladder_30_ci_1, fulladder_31_ci_1,
       fulladder_32_ci_1;

  fulladder fulladder_1 (.A(B[31]), .B(A[31]), .Sum(Res[31]), .Ci(fulladder_3_ci_1));  // open: Ci_1
  fulladder fulladder_2 (.A(B[29]), .B(A[29]), .Sum(Res[29]), .Ci_1(fulladder_2_ci_1), .Ci(fulladder_4_ci_1));
  fulladder fulladder_3 (.A(B[30]), .B(A[30]), .Sum(Res[30]), .Ci_1(fulladder_3_ci_1), .Ci(fulladder_2_ci_1));
  fulladder fulladder_4 (.A(B[28]), .B(A[28]), .Sum(Res[28]), .Ci_1(fulladder_4_ci_1), .Ci(fulladder_5_ci_1));
  fulladder fulladder_5 (.A(B[27]), .B(A[27]), .Sum(Res[27]), .Ci_1(fulladder_5_ci_1), .Ci(fulladder_7_ci_1));
  fulladder fulladder_6 (.A(B[25]), .B(A[25]), .Sum(Res[25]), .Ci_1(fulladder_6_ci_1), .Ci(fulladder_8_ci_1));
  fulladder fulladder_7 (.A(B[26]), .B(A[26]), .Sum(Res[26]), .Ci_1(fulladder_7_ci_1), .Ci(fulladder_6_ci_1));
  fulladder fulladder_8 (.A(B[24]), .B(A[24]), .Sum(Res[24]), .Ci_1(fulladder_8_ci_1), .Ci(fulladder_9_ci_1));
  fulladder fulladder_9 (.A(B[23]), .B(A[23]), .Sum(Res[23]), .Ci_1(fulladder_9_ci_1), .Ci(fulladder_11_ci_1));
  fulladder fulladder_10 (.A(B[21]), .B(A[21]), .Sum(Res[21]), .Ci_1(fulladder_10_ci_1), .Ci(fulladder_13_ci_1));
  fulladder fulladder_11 (.A(B[22]), .B(A[22]), .Sum(Res[22]), .Ci_1(fulladder_11_ci_1), .Ci(fulladder_10_ci_1));
  fulladder fulladder_12 (.A(B[19]), .B(A[19]), .Sum(Res[19]), .Ci_1(fulladder_12_ci_1), .Ci(fulladder_14_ci_1));
  fulladder fulladder_13 (.A(B[20]), .B(A[20]), .Sum(Res[20]), .Ci_1(fulladder_13_ci_1), .Ci(fulladder_12_ci_1));
  fulladder fulladder_14 (.A(B[18]), .B(A[18]), .Sum(Res[18]), .Ci_1(fulladder_14_ci_1), .Ci(fulladder_15_ci_1));
  fulladder fulladder_15 (.A(B[17]), .B(A[17]), .Sum(Res[17]), .Ci_1(fulladder_15_ci_1), .Ci(fulladder_17_ci_1));
  fulladder fulladder_16 (.A(B[15]), .B(A[15]), .Sum(Res[15]), .Ci_1(fulladder_16_ci_1), .Ci(fulladder_19_ci_1));
  fulladder fulladder_17 (.A(B[16]), .B(A[16]), .Sum(Res[16]), .Ci_1(fulladder_17_ci_1), .Ci(fulladder_16_ci_1));
  fulladder fulladder_18 (.A(B[13]), .B(A[13]), .Sum(Res[13]), .Ci_1(fulladder_18_ci_1), .Ci(fulladder_21_ci_1));
  fulladder fulladder_19 (.A(B[14]), .B(A[14]), .Sum(Res[14]), .Ci_1(fulladder_19_ci_1), .Ci(fulladder_18_ci_1));
  fulladder fulladder_20 (.A(B[11]), .B(A[11]), .Sum(Res[11]), .Ci_1(fulladder_20_ci_1), .Ci(fulladder_22_ci_1));
  fulladder fulladder_21 (.A(B[12]), .B(A[12]), .Sum(Res[12]), .Ci_1(fulladder_21_ci_1), .Ci(fulladder_20_ci_1));
  fulladder fulladder_22 (.A(B[10]), .B(A[10]), .Sum(Res[10]), .Ci_1(fulladder_22_ci_1), .Ci(fulladder_23_ci_1));
  fulladder fulladder_23 (.A(B[9]), .B(A[9]), .Sum(Res[9]), .Ci_1(fulladder_23_ci_1), .Ci(fulladder_24_ci_1));
  fulladder fulladder_24 (.A(B[8]), .B(A[8]), .Sum(Res[8]), .Ci_1(fulladder_24_ci_1), .Ci(fulladder_25_ci_1));
  fulladder fulladder_25 (.A(B[7]), .B(A[7]), .Sum(Res[7]), .Ci_1(fulladder_25_ci_1), .Ci(fulladder_26_ci_1));
  fulladder fulladder_26 (.A(B[6]), .B(A[6]), .Sum(Res[6]), .Ci_1(fulladder_26_ci_1), .Ci(fulladder_27_ci_1));
  fulladder fulladder_27 (.A(B[5]), .B(A[5]), .Sum(Res[5]), .Ci_1(fulladder_27_ci_1), .Ci(fulladder_29_ci_1));
  fulladder fulladder_28 (.A(B[3]), .B(A[3]), .Sum(Res[3]), .Ci_1(fulladder_28_ci_1), .Ci(fulladder_31_ci_1));
  fulladder fulladder_29 (.A(B[4]), .B(A[4]), .Sum(Res[4]), .Ci_1(fulladder_29_ci_1), .Ci(fulladder_28_ci_1));
  fulladder fulladder_30 (.A(B[1]), .B(A[1]), .Sum(Res[1]), .Ci_1(fulladder_30_ci_1), .Ci(fulladder_32_ci_1));
  fulladder fulladder_31 (.A(B[2]), .B(A[2]), .Sum(Res[2]), .Ci_1(fulladder_31_ci_1), .Ci(fulladder_30_ci_1));
  fulladder fulladder_32 (.A(B[0]), .B(A[0]), .Sum(Res[0]), .Ci_1(fulladder_32_ci_1), .Ci(Ci));
endmodule

// Shifter
module _32bitshifter (
  input  flag,
  input  [31:0] \input ,
  output [31:0] \output 
);

  wire and_1_out, and_3_out, and_4_out, and_5_out, and_6_out, and_7_out, and_8_out, and_9_out, and_10_out,
       and_11_out, and_12_out, and_13_out, and_14_out, and_15_out, and_16_out, and_17_out, and_18_out,
       and_19_out, and_20_out, and_21_out, and_22_out, and_23_out, and_24_out, and_25_out, and_26_out,
       and_27_out, and_28_out, and_29_out, and_30_out, and_31_out, and_32_out, and_33_out, and_34_out,
       and_35_out, and_36_out, and_37_out, and_38_out, and_39_out, and_40_out, and_41_out, and_42_out,
       and_43_out, and_44_out, and_45_out, and_46_out, and_47_out, and_48_out, and_49_out, and_50_out,
       and_51_out, and_52_out, and_53_out, and_54_out, and_55_out, and_56_out, and_57_out, and_58_out,
       and_59_out, and_60_out, and_62_out, not_1_out;

  not not_1 (not_1_out, flag);
  and and_1 (and_1_out, \input [0], flag);
  and and_2 (\output [0], not_1_out, \input [1]);
  and and_3 (and_3_out, \input [1], flag);
  and and_4 (and_4_out, not_1_out, \input [2]);
  and and_5 (and_5_out, \input [2], flag);
  and and_6 (and_6_out, not_1_out, \input [3]);
  and and_7 (and_7_out, \input [3], flag);
  and and_8 (and_8_out, not_1_out, \input [4]);
  and and_9 (and_9_out, \input [4], flag);
  and and_10 (and_10_out, not_1_out, \input [5]);
  and and_11 (and_11_out, \input [5], flag);
  and and_12 (and_12_out, not_1_out, \input [6]);
  and and_13 (and_13_out, \input [6], flag);
  and and_14 (and_14_out, not_1_out, \input [7]);
  and and_15 (and_15_out, \input [7], flag);
  and and_16 (and_16_out, not_1_out, \input [8]);
  and and_17 (and_17_out, \input [8], flag);
  and and_18 (and_18_out, not_1_out, \input [9]);
  and and_19 (and_19_out, \input [9], flag);
  and and_20 (and_20_out, not_1_out, \input [10]);
  and and_21 (and_21_out, \input [10], flag);
  and and_22 (and_22_out, not_1_out, \input [11]);
  and and_23 (and_23_out, \input [11], flag);
  and and_24 (and_24_out, not_1_out, \input [12]);
  and and_25 (and_25_out, \input [12], flag);
  and and_26 (and_26_out, not_1_out, \input [13]);
  and and_27 (and_27_out, \input [13], flag);
  and and_28 (and_28_out, not_1_out, \input [14]);
  and and_29 (and_29_out, \input [14], flag);
  and and_30 (and_30_out, not_1_out, \input [15]);
  and and_31 (and_31_out, \input [15], flag);
  and and_32 (and_32_out, not_1_out, \input [16]);
  and and_33 (and_33_out, \input [16], flag);
  and and_34 (and_34_out, not_1_out, \input [17]);
  and and_35 (and_35_out, \input [17], flag);
  and and_36 (and_36_out, not_1_out, \input [18]);
  and and_37 (and_37_out, \input [18], flag);
  and and_38 (and_38_out, not_1_out, \input [19]);
  and and_39 (and_39_out, \input [19], flag);
  and and_40 (and_40_out, not_1_out, \input [20]);
  and and_41 (and_41_out, \input [20], flag);
  and and_42 (and_42_out, not_1_out, \input [21]);
  and and_43 (and_43_out, \input [21], flag);
  and and_44 (and_44_out, not_1_out, \input [22]);
  and and_45 (and_45_out, \input [22], flag);
  and and_46 (and_46_out, not_1_out, \input [23]);
  and and_47 (and_47_out, \input [23], flag);
  and and_48 (and_48_out, not_1_out, \input [24]);
  and and_49 (and_49_out, \input [24], flag);
  and and_50 (and_50_out, not_1_out, \input [25]);
  and and_51 (and_51_out, \input [25], flag);
  and and_52 (and_52_out, not_1_out, \input [26]);
  and and_53 (and_53_out, \input [26], flag);
  and and_54 (and_54_out, not_1_out, \input [27]);
  and and_55 (and_55_out, \input [27], flag);
  and and_56 (and_56_out, not_1_out, \input [28]);
  and and_57 (and_57_out, \input [28], flag);
  and and_58 (and_58_out, not_1_out, \input [29]);
  and and_59 (and_59_out, \input [29], flag);
  and and_60 (and_60_out, not_1_out, \input [30]);
  and and_61 (\output [31], \input [30], flag);
  and and_62 (and_62_out, \input [31], not_1_out);
  or or_1 (\output [1], and_1_out, and_4_out);
  or or_2 (\output [2], and_3_out, and_6_out);
  or or_3 (\output [3], and_5_out, and_8_out);
  or or_4 (\output [4], and_7_out, and_10_out);
  or or_5 (\output [5], and_9_out, and_12_out);
  or or_6 (\output [6], and_11_out, and_14_out);
  or or_7 (\output [7], and_13_out, and_16_out);
  or or_8 (\output [8], and_15_out, and_18_out);
  or or_9 (\output [9], and_17_out, and_20_out);
  or or_10 (\output [10], and_19_out, and_22_out);
  or or_11 (\output [11], and_21_out, and_24_out);
  or or_12 (\output [12], and_23_out, and_26_out);
  or or_13 (\output [13], and_25_out, and_28_out);
  or or_14 (\output [14], and_27_out, and_30_out);
  or or_15 (\output [15], and_29_out, and_32_out);
  or or_16 (\output [16], and_31_out, and_34_out);
  or or_17 (\output [17], and_33_out, and_36_out);
  or or_18 (\output [18], and_35_out, and_38_out);
  or or_19 (\output [19], and_37_out, and_40_out);
  or or_20 (\output [20], and_39_out, and_42_out);
  or or_21 (\output [21], and_41_out, and_44_out);
  or or_22 (\output [22], and_43_out, and_46_out);
  or or_23 (\output [23], and_45_out, and_48_out);
  or or_24 (\output [24], and_47_out, and_50_out);
  or or_25 (\output [25], and_49_out, and_52_out);
  or or_26 (\output [26], and_51_out, and_54_out);
  or or_27 (\output [27], and_53_out, and_56_out);
  or or_28 (\output [28], and_55_out, and_55_out, and_58_out);
  or or_29 (\output [29], and_57_out, and_60_out);
  or or_30 (\output [30], and_59_out, and_62_out);
endmodule

// Setter
module msbsetter (
  input  [31:0] \input ,
  input  Flag,
  output [31:0] \output 
);

  wire not_1_out;
  wire [31:0] or_1_out;

  assign or_1_out = \input  | 32'h80000000;  // OR_Gate or_1, 32 bits wide
  not not_1 (not_1_out, Flag);
  Multiplexer #(.width(32), .enable("false")) multiplexer_1 (
    .in0(or_1_out), .in1(\input ), .out(\output ), .sel(not_1_out));
endmodule
