// Logisim project mult32.circ as structural Verilog: 1 circuit, main circuit main
module main (
  input  [7:0] in_1,
  input  [7:0] in_2,
  input  [7:0] in_3,
  input  [7:0] LSB,
  input  [7:0] in_5,
  input  [7:0] in_6,
  input  [7:0] in_7,
  input  [7:0] LSB_2,
  input  Enable,
  output [7:0] Counter,
  output [7:0] MSB,
  output [7:0] out_12,
  output [7:0] out_13,
  output [7:0] out_14,
  output [7:0] out_15,
  output [7:0] out_16,
  output [7:0] out_17,
  output [7:0] out_18
);

  wire Clear_out, Clock_out, Set_out;

  Button Set (.out(Set_out));
  Button Clear (.out(Clear_out));
  Clock Clock (.out(Clock_out));
  datapath_main main_1 (
    .Set(Set_out), .Counter(Counter), .LSB({out_15, out_16, out_17, out_18}),
    .MSB({MSB, out_12, out_13, out_14}), .Multiplicand({in_1, in_2, in_3, LSB}),
    .Multiplier({in_5, in_6, in_7, LSB_2}), .Clock(Enable), .Clear(Clear_out), .Enable(Clock_out));

  // Notes on the sheet:
  //   Multiplier
  //   MSB
  //   Product
  //   Multiplicand
  //   MSB
  //   LSB
endmodule
